# Fritzing sketch bulk_chip (saved by Fritzing 0.9.3b)
breadboards: 1

parts:
  KIT_XMC11_BOOT_1 = Boot Kit XMC1100 [part_number=KITXMC11BOOT001TOBO1]
  IC1 = SO08w [chip_label=TLE5012B package=SO(w)]  # not connected
  IC2 = SO-24x [chip_label=IC package=SO(x)]  # not connected
  IC3 = SO-28W [chip_label=TLE5012 package=SO(w)]  # not connected
  IC4 = SO08w [chip_label=IC package=SO(w)]  # not connected
  IC5 = SO08w [chip_label=IC package=SO(w)]  # not connected
  R1 = Resistor [tolerance=±5% resistance=470 package="1206 [SMD]"]
  IC6 = IC, DIP package, 8 pins [chip_label=TLE5012B]

nets:
  N1: KIT_XMC11_BOOT_1.P0.9, IC6.pin3
  N2: KIT_XMC11_BOOT_1.P1.1, KIT_XMC11_BOOT_1.P1.0, R1.Pin_0
  N3: KIT_XMC11_BOOT_1.P0.7, IC6.pin2
  N4: KIT_XMC11_BOOT_1.GND, IC6.pin7
  N5: KIT_XMC11_BOOT_1.+3V3_DEV, IC6.pin6
  N6: R1.Pin_1, IC6.pin4

custom parts:
  Boot Kit XMC1100: The XMC1100 CPU Card for Arduino TM has two rows of pin headers which fully compatible with Arduino TM shield. Hence, user can buy various Arduino shield boards off - the - shelf to test the capabilities of XMC1100 Microcontroller. Summary of Features: XMC1100 Microcontroller in TSSOP-38 with 64 KB Flash and full peripheral set of XMC1100 series Detachable SEGGER J-Link Board shape & power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
